// Logisim project cpu.circ as structural Verilog: 1 circuit, main circuit cpu
module cpu (
  input  clk,
  input  [31:0] INSTRUCTION,
  input  [31:0] READ_DATA,
  output [31:0] WRITE_ADDRESS,
  output [31:0] PROGRAM_COUNTER,
  output [31:0] ra,
  output [31:0] sp,
  output [31:0] t0,
  output [31:0] t1,
  output [31:0] t2,
  output [31:0] s0,
  output [31:0] s1,
  output [31:0] a0,
  output [31:0] tohost,
  output [3:0] WRITE_ENABLE,
  output [31:0] WRITE_DATA
);

  wire [2:0] funct3;
  wire [31:0] adder_1_out, ALU_result, imm_src, INSTRUCTION2, src1, src2, WB_data;

  Adder #(.width(32)) adder_1 (.a(PROGRAM_COUNTER), .b(32'h4), .out(adder_1_out));  // open: cin, cout
  Register #(.width(32)) PC (.D(adder_1_out), .clk(clk), .Q(PROGRAM_COUNTER));  // open: en, clr
  Register #(.width(32)) register_1 (
    .D(INSTRUCTION), .clk(clk), .Q({INSTRUCTION2[31:15], funct3, INSTRUCTION2[11:0]}));  // open: en, clr
  // branch_comp branch_comp_1: pin names not known
  // control_logic control_logic_1: pin names not known
  Multiplexer #(.enable("false"), .select(2), .width(32)) multiplexer_1 (
    .in0(READ_DATA), .in1(ALU_result), .out(WB_data), .sel(2'b01));  // open: in2, in3
  imm_gen imm_gen_1 (.inst({INSTRUCTION2[31:15], funct3, INSTRUCTION2[11:0]}), .ImmSel(3'b000), .imm(imm_src));
  regfile regfile_1 (
    .rs1(INSTRUCTION2[19:15]), .rd(INSTRUCTION2[11:7]), .Write_Data(WB_data), .RegWEn(1'b1), .clk(clk),
    .ra(ra), .sp(sp), .t0(t0), .t1(t1), .t2(t2), .s0(s0), .s1(s1), .a0(a0), .Read_Data_1(src1),
    .Read_Data_2(src2));  // open: rs2
  alu alu_1 (.Result(ALU_result), .A(src1), .B(imm_src), .ALUSel(4'b0000));
  csr csr_1 (.tohost(tohost));  // open: CSR_address, CSR_din, CSR_WE, clk

  // Other names for the same wires on the sheet: opcode[6:0] = INSTRUCTION2[6:0]; rd[4:0] = INSTRUCTION2[11:7];
  //   INSTRUCTION2[14:12] = funct3; rs1[4:0] = INSTRUCTION2[19:15]; unused_imm[11:0] = INSTRUCTION2[31:20]

  // Notes on the sheet:
  //   MEM
  //   IF
  //   Output to IMEM
  //   IMEM (do **NOT** move this)
  //   Inputs from IMEM
  //   ID
  //   WB
  //   Inputs/Outputs for testing. Do **NOT** move these.
  //   EX
  //   Outputs To DMEM
  //   DMEM (do **NOT** move this)
  //   Inputs From DMEM
endmodule
